// Digital circuit DEMULTIPLEXOR 4 SALIDAS.dig as structural Verilog
module DEMULTIPLEXOR_4_SALIDAS (
  input  Sel_1,
  input  Sel_0,
  input  Entrada,
  output Out0,
  output Out1,
  output Out2,
  output Out3
);

  wire not_1_out, not_2_out;

  not not_1 (not_1_out, Sel_1);
  not not_2 (not_2_out, Sel_0);
  and and_1 (Out0, Entrada, Sel_1, Sel_0);
  and and_2 (Out1, Entrada, not_1_out, Sel_0);
  and and_3 (Out2, Entrada, Sel_1, not_2_out);
  and and_4 (Out3, Entrada, not_1_out, not_2_out);

  // Notes on the sheet:
  //   ENCENDER 0-1
  //   ENCENDER 0
  //   ENCENDER 1
  //   APAGAR TODO
endmodule
