// Digital circuit FLIP FLOP.dig as structural Verilog
module FLIP_FLOP (
  input  in_1,
  input  in_2,
  input  in_3,
  input  in_4,
  input  clk,
  input  clk_2,
  input  K,
  input  Clock,
  input  J,
  input  Set,
  input  Reset,
  input  Clock_2,
  output out_5,
  output out_6,
  output out_7,
  output out_8,
  output Q,
  output Q_2,
  output Q_3,
  output Q_4
);

  wire nand_1_out, nand_2_out, nand_3_out, nand_4_out, nand_5_out, nand_6_out, nand_9_out, nand_10_out,
       nand_11_out, nand_12_out, nand_13_out, nand_14_out, not_1_out, not_2_out;

  not not_1 (not_1_out, Clock_2);
  nand nand_1 (nand_1_out, Set, not_1_out);
  nand nand_2 (nand_2_out, not_1_out, Reset);
  RS_FF rs_ff_1 (.S(in_1), .C(clk), .R(in_2), .Q(out_5), .nQ(out_6));
  nand nand_3 (nand_3_out, nand_1_out, nand_4_out);
  nand nand_4 (nand_4_out, nand_3_out, nand_2_out);
  nand nand_5 (nand_5_out, nand_3_out, Clock_2);
  nand nand_6 (nand_6_out, Clock_2, nand_4_out);
  nand nand_7 (Q_3, nand_5_out, Q_4);
  nand nand_8 (Q_4, Q_3, nand_6_out);
  nand nand_9 (nand_9_out, J, Q_2, Clock);
  nand nand_10 (nand_10_out, Clock, Q, K);
  nand nand_11 (nand_11_out, nand_9_out, nand_12_out);
  nand nand_12 (nand_12_out, nand_11_out, nand_10_out);
  not not_2 (not_2_out, Clock);
  JK_FF jk_ff_1 (.J(in_3), .C(clk_2), .K(in_4), .Q(out_7), .nQ(out_8));
  nand nand_13 (nand_13_out, nand_11_out, not_2_out);
  nand nand_14 (nand_14_out, not_2_out, nand_12_out);
  nand nand_15 (Q, nand_13_out, Q_2);
  nand nand_16 (Q_2, Q, nand_14_out);

  // Notes on the sheet:
  //   Este esquema fue realizado con compuertas Nand,  contienen un elemento llamado Clock, el cual nos permite enviar periodicamente las respectivas señales,
  //   si este se encuentra activo funciona como un pulso cuadrado, refrescando de este modo la informacion del reset y el set.
  //   Finalemte esta configuracion del flip-flop  RS tiene diferentes comandos:
  //   cuando el Set toma valor de 1, y el reset de 0, la salida de Q sera 1,
  //   si el reset es 1 y el set 0, limpia la señal, volviendo 0 a Q, 
  //   si ambas entradas son 0, el sistema toma el valor anterior a este, como  una memoria, 
  //   y si ambos son 1,  la respuesta es indefinida ya que no se puede predecir cual de las dos posibles salidas se va a encender
  //   FLIP FLOP RS
  //   Este esquema fue realizado con compuertas Nand,  contienen un elemento llamado Clock, el cual nos permite enviar periodicamente las respectivas señales,
  //   si este se encuentra activo funciona como un pulso cuadrado, refrescando de este modo la informacion del reset y el set.
  //   Finalemte esta configuracion del flip-flop  JK tiene diferentes comandos:
  //   cuando el Set toma valor de 1, y el reset de 0, la salida de Q sera 1,
  //   si el reset es 1 y el set 0, limpia la señal, volviendo 0 a Q, 
  //   si ambas entradas son 0, el sistema toma el valor anterior a este, como  una memoria, 
  //   y a diferencia del flip-flop RS cuando ambos toman el valor de 1, este toma un estado oscilatorio, cambiando de salida secuencialmente cada que el clock emite nuevamente la señal,
  //   corrigiendo asi el error de probabilidad en las salidas del anterior
  //   FLIP FLOP JK
endmodule
