// Digital circuit MULTIPLEXOR DE 8 ENTRADAS.dig as structural Verilog
module MULTIPLEXOR_DE_8_ENTRADAS (
  input  I7,
  input  I6,
  input  I5,
  input  I4,
  input  I3,
  input  I2,
  input  I1,
  input  I0,
  input  Sel2,
  input  Sel1,
  input  Sel0,
  output out_12
);

  wire and_1_out, and_2_out, and_3_out, and_4_out, and_5_out, and_6_out, and_7_out, and_8_out, not_1_out,
       not_2_out, not_3_out, or_1_out, or_2_out;

  not not_1 (not_1_out, Sel2);
  not not_2 (not_2_out, Sel1);
  not not_3 (not_3_out, Sel0);
  and and_1 (and_1_out, I7, Sel2, Sel1, Sel0);
  and and_2 (and_2_out, I6, not_1_out, Sel1, Sel0);
  and and_3 (and_3_out, I5, Sel2, not_2_out, Sel0);
  and and_4 (and_4_out, I4, Sel2, Sel1, not_3_out);
  and and_5 (and_5_out, I3, not_1_out, not_2_out, Sel0);
  and and_6 (and_6_out, I2, Sel2, not_2_out, not_3_out);
  and and_7 (and_7_out, I1, not_1_out, Sel1, not_3_out);
  and and_8 (and_8_out, I0, not_1_out, not_2_out, not_3_out);
  or or_1 (or_1_out, and_1_out, and_2_out, and_3_out, and_4_out);
  or or_2 (or_2_out, and_5_out, and_6_out, and_7_out, and_8_out);
  or or_3 (out_12, or_1_out, or_2_out);

  // Notes on the sheet:
  //   ENCENDER 0-1-2
  //   ENCENDER 0-1
  //   ENCENDER 0-2
  //   ENCENDER 1-2
  //   ENCENDER 0
  //   ENCENDER 2
  //   ENCENDER 1
  //   APAGAR TODO
endmodule
