// Digital circuit REGISTRO.dig as structural Verilog
module REGISTRO (
  input  Clear,
  input  D1,
  input  Enable,
  input  D2,
  input  D3,
  input  D4,
  input  Set,
  input  Clock,
  input  I1ON,
  input  SetD1,
  input  SetD1_2,
  input  I1OFF,
  input  I2ON,
  input  SetD2,
  input  SetD2_2,
  input  I2OFF,
  input  I3ON,
  input  SetD3,
  input  SetD3_2,
  input  I3OFF,
  input  I4ON,
  input  SetD4,
  input  SetD4_2,
  input  I4OFF,
  output out_9,
  output out_12,
  output out_15,
  output out_18,
  output out_21,
  output out_24,
  output out_27,
  output out_30
);

  wire d_ff_as_1_q, d_ff_as_4_q, d_ff_as_10_q, d_ff_as_11_q, driver_1_out, driver_2_out, driver_3_out,
       driver_4_out, multiplexer_1_out, multiplexer_2_out, multiplexer_3_out, multiplexer_4_out,
       multiplexer_5_out, multiplexer_6_out, multiplexer_7_out, multiplexer_8_out, multiplexer_9_out,
       multiplexer_10_out, multiplexer_11_out, multiplexer_12_out, Out1, Out2, Out3, Out4;

  assign driver_1_out = Out1 ? I1ON : 1'bz;  // Driver driver_1
  assign out_9 = ~Out1 ? d_ff_as_1_q : 1'bz;  // DriverInvSel driverinvsel_1
  Multiplexer multiplexer_1 (.sel(Enable), .in_0(out_12), .in_1(driver_1_out), .out(multiplexer_1_out));
  D_FF_AS d_ff_as_1 (.Set(SetD1_2), .D(multiplexer_2_out), .C(Clock), .Clr(Clear), .Q(d_ff_as_1_q));  // open: nQ
  D_FF_AS d_ff_as_2 (.Set(SetD1), .D(multiplexer_1_out), .C(Clock), .Clr(Clear), .Q(out_12));  // open: nQ
  Multiplexer multiplexer_2 (.sel(Enable), .in_0(d_ff_as_1_q), .in_1(I1OFF), .out(multiplexer_2_out));
  Multiplexer multiplexer_3 (.sel(Enable), .in_0(Out1), .in_1(D1), .out(multiplexer_3_out));
  D_FF_AS d_ff_as_3 (.Set(Set), .D(multiplexer_3_out), .C(Clock), .Clr(Clear), .Q(Out1));  // open: nQ
  assign driver_2_out = Out2 ? I2ON : 1'bz;  // Driver driver_2
  assign out_15 = ~Out2 ? d_ff_as_4_q : 1'bz;  // DriverInvSel driverinvsel_2
  Multiplexer multiplexer_4 (.sel(Enable), .in_0(out_18), .in_1(driver_2_out), .out(multiplexer_4_out));
  Multiplexer multiplexer_5 (.sel(Enable), .in_0(Out2), .in_1(D2), .out(multiplexer_5_out));
  D_FF_AS d_ff_as_4 (.Set(SetD2_2), .D(multiplexer_6_out), .C(Clock), .Clr(Clear), .Q(d_ff_as_4_q));  // open: nQ
  D_FF_AS d_ff_as_5 (.Set(SetD2), .D(multiplexer_4_out), .C(Clock), .Clr(Clear), .Q(out_18));  // open: nQ
  D_FF_AS d_ff_as_6 (.Set(Set), .D(multiplexer_5_out), .C(Clock), .Clr(Clear), .Q(Out2));  // open: nQ
  Multiplexer multiplexer_6 (.sel(Enable), .in_0(d_ff_as_4_q), .in_1(I2OFF), .out(multiplexer_6_out));
  Multiplexer multiplexer_7 (.sel(Enable), .in_0(Out3), .in_1(D3), .out(multiplexer_7_out));
  D_FF_AS d_ff_as_7 (.Set(Set), .D(multiplexer_7_out), .C(Clock), .Clr(Clear), .Q(Out3));  // open: nQ
  assign driver_3_out = Out3 ? I3ON : 1'bz;  // Driver driver_3
  assign out_21 = ~Out3 ? d_ff_as_10_q : 1'bz;  // DriverInvSel driverinvsel_3
  Multiplexer multiplexer_8 (.sel(Enable), .in_0(Out4), .in_1(D4), .out(multiplexer_8_out));
  Multiplexer multiplexer_9 (.sel(Enable), .in_0(out_24), .in_1(driver_3_out), .out(multiplexer_9_out));
  D_FF_AS d_ff_as_8 (.Set(Set), .D(multiplexer_8_out), .C(Clock), .Clr(Clear), .Q(Out4));  // open: nQ
  D_FF_AS d_ff_as_9 (.Set(SetD3), .D(multiplexer_9_out), .C(Clock), .Clr(Clear), .Q(out_24));  // open: nQ
  D_FF_AS d_ff_as_10 (.Set(SetD3_2), .D(multiplexer_10_out), .C(Clock), .Clr(Clear), .Q(d_ff_as_10_q));  // open: nQ
  Multiplexer multiplexer_10 (.sel(Enable), .in_0(d_ff_as_10_q), .in_1(I3OFF), .out(multiplexer_10_out));
  assign driver_4_out = Out4 ? I4ON : 1'bz;  // Driver driver_4
  assign out_27 = ~Out4 ? d_ff_as_11_q : 1'bz;  // DriverInvSel driverinvsel_4
  Multiplexer multiplexer_11 (.sel(Enable), .in_0(out_30), .in_1(driver_4_out), .out(multiplexer_11_out));
  D_FF_AS d_ff_as_11 (.Set(SetD4_2), .D(multiplexer_12_out), .C(Clock), .Clr(Clear), .Q(d_ff_as_11_q));  // open: nQ
  D_FF_AS d_ff_as_12 (.Set(SetD4), .D(multiplexer_11_out), .C(Clock), .Clr(Clear), .Q(out_30));  // open: nQ
  Multiplexer multiplexer_12 (.sel(Enable), .in_0(d_ff_as_11_q), .in_1(I4OFF), .out(multiplexer_12_out));

  // Notes on the sheet:
  //   Clock: Hz: 5
  //   I1ON: default 1
  //   I1OFF: default 1
  //   I2ON: default 1
  //   I2OFF: default 1
  //   I3ON: default 1
  //   I3OFF: default 1
  //   I4ON: default 1
  //   I4OFF: default 1
  //   REGISTRO DE ESTADO PARA ENTRADA
  //   REGISTRO DE DE PIN DE SALIDA
  //   REGISTRO DE CONFIGURACION
endmodule
